# Fritzing sketch sketch (saved by Fritzing 0.9.4)
breadboards: 1

parts:
  U1 = ESP32S-HiLetgo [part_number=ESP32S-HiLetgo]
  U2 = TMP36 [package=to-92-kit]
  JP1 = Jumper [package=sj_2s-no-ns]
  U4 = LIPO-110mAh [package=lipo-110]
  TP1 = TP4056 [chip_label=TP4056 package="DIP (Dual Inline) [THT]"]
  R1 = Resistor [tolerance=±1% resistance=1M package=THT]
  R2 = Resistor [tolerance=±1% resistance=1M package=THT]

nets:
  N1: U1.3.3, U2.VCC
  N2: U1.GPIO34, U2.VOUT
  GND: U1.GND, U2.GND, JP1.1, TP1.pin6, R2.Pin_1
  N3: U1.VIN, TP1.pin3, R1.Pin_1
  N4: U1.GPIO4, R1.Pin_0, R2.Pin_0
  N5: U1.GPIO16, JP1.2
  N6: U4.+, TP1.pin4
  N7: U4.-, TP1.pin5

custom parts:
  ESP32S-HiLetgo: HiLetgo ESP-WROOM-32 ESP32 ESP-32S Development Board 2.4GHz Dual-Mode WiFi + Bluetooth Dual Cores Microcontroller The ESP32 integrated with Antenna switches, RF Balun, power amplifiers, low-noise amplifiers, filters, and management modules, and the entire solution occupies the least area of PCB. 2.4 GHz Wi-Fi plus Bluetooth dual-mode chip, with TSMC Ultra-low power consumption 40nm technology,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
  TP4056: A DIP stand-in part for whatever IC you want. With 6 pins on a 300mil dual inline package (DIP) footprint.
